// Logisim project factorial_bug.circ as structural Verilog: 1 circuit, main circuit Factorial_Circuit_5e3a82b1
module Factorial_Circuit_5e3a82b1 (
  output [15:0] n_Factorial
);

  wire clock_1_out, d_ff_1_qn;
  wire [15:0] multiplexer_1_out, N_minus_1_q, n_q;

  Clock clock_1 (.out(clock_1_out));
  D_Flip_Flop d_ff_1 (.D(1'b1), .clk(clock_1_out), .Qn(d_ff_1_qn));  // open: Q, preset, reset
  Multiplexer #(.width(16)) multiplexer_1 (.in0(n_q), .in1(16'h1), .out(multiplexer_1_out), .sel(d_ff_1_qn));
  Register #(.width(16)) n (.D(n_Factorial), .clk(clock_1_out), .Q(n_q));  // open: en, clr
  Register #(.width(16)) N_minus_1 (.D(multiplexer_1_out), .clk(clock_1_out), .Q(N_minus_1_q));  // open: en, clr
  Adder #(.width(16)) adder_1 (.a(n_q), .b(N_minus_1_q), .out(n_Factorial));  // open: cin, cout

  // Notes on the sheet:
  //   Factorial circuit
endmodule
